// Logisim project PSD - LAB 06 - ALDEN LUTHFI - 2206028932.circ as structural Verilog: 1 circuit, main circuit main
module main (
  input  A,
  output O
);

  wire clock_1_out, DY_q, JKX_q, or_1_out, xnor_1_out;

  Clock clock_1 (.out(clock_1_out));
  or or_1 (or_1_out, A, DY_q);
  xnor xnor_1 (xnor_1_out, A, DY_q);
  J_K_Flip_Flop JKX (.J(or_1_out), .clk(clock_1_out), .K(or_1_out), .Q(JKX_q));  // open: Qn, preset, en, reset
  D_Flip_Flop DY (.clk(clock_1_out), .D(xnor_1_out), .Q(DY_q));  // open: Qn, preset, en, reset
  and and_1 (O, JKX_q, or_1_out);
endmodule
