// Logisim project PSD - TUGAS MANDIRI 6 - ALDEN LUTHFI - 2206028932.circ as structural Verilog: 3 circuits, main circuit No. 2 (Version 1)
module No__2__Version_1 (
  input  X,
  output Y,
  output P,
  output Q,
  output R,
  output S
);

  wire and_1_out, and_2_out, and_3_out, and_4_out, and_5_out, and_6_out, and_7_out, and_8_out, and_9_out,
       and_10_out, and_11_out, and_12_out, and_13_out, and_14_out, and_15_out, and_16_out, and_17_out,
       and_18_out, and_19_out, and_20_out, and_21_out, and_22_out, clock_1_out, not_1_out, not_2_out,
       not_3_out, not_4_out, not_5_out, not_6_out, not_7_out, not_8_out, not_9_out, not_10_out, not_11_out,
       not_12_out, not_13_out, not_14_out, not_15_out, not_16_out, not_17_out, not_18_out, not_19_out,
       not_20_out, not_21_out, not_22_out, not_23_out, not_24_out, not_25_out, not_26_out, not_27_out,
       or_2_out, or_3_out, or_4_out, or_5_out;

  not not_1 (not_1_out, R);
  not not_2 (not_2_out, X);
  not not_3 (not_3_out, P);
  not not_4 (not_4_out, Q);
  not not_5 (not_5_out, R);
  not not_6 (not_6_out, X);
  not not_7 (not_7_out, S);
  not not_8 (not_8_out, X);
  not not_9 (not_9_out, R);
  not not_10 (not_10_out, S);
  not not_11 (not_11_out, X);
  not not_12 (not_12_out, Q);
  not not_13 (not_13_out, S);
  not not_14 (not_14_out, R);
  not not_15 (not_15_out, X);
  not not_16 (not_16_out, R);
  not not_17 (not_17_out, X);
  not not_18 (not_18_out, Q);
  not not_19 (not_19_out, S);
  not not_20 (not_20_out, X);
  not not_21 (not_21_out, R);
  not not_22 (not_22_out, X);
  not not_23 (not_23_out, Q);
  not not_24 (not_24_out, R);
  not not_25 (not_25_out, S);
  not not_26 (not_26_out, Q);
  not not_27 (not_27_out, S);
  and and_1 (and_1_out, Q, not_1_out);
  and and_2 (and_2_out, P, R);
  and and_3 (and_3_out, not_2_out, not_3_out, not_4_out, not_5_out);
  and and_4 (and_4_out, not_6_out, Q, R, not_7_out);
  and and_5 (and_5_out, P, R);
  and and_6 (and_6_out, not_8_out, R, S);
  and and_7 (and_7_out, Q, not_9_out, not_10_out);
  and and_8 (and_8_out, not_11_out, P);
  and and_9 (and_9_out, P, R);
  and and_10 (and_10_out, X, Q, R);
  and and_11 (and_11_out, not_12_out, R, not_13_out);
  and and_12 (and_12_out, Q, not_14_out);
  and and_13 (and_13_out, Q, S);
  and and_14 (and_14_out, not_15_out, P);
  and and_15 (and_15_out, P, R);
  and and_16 (and_16_out, X, not_16_out, S);
  and and_17 (and_17_out, not_17_out, not_18_out, R, not_19_out);
  and and_18 (and_18_out, not_20_out, Q, not_21_out);
  and and_19 (and_19_out, not_22_out, Q, S);
  and and_20 (and_20_out, X, not_23_out, not_24_out, not_25_out);
  and and_21 (and_21_out, X, not_26_out, R, S);
  and and_22 (and_22_out, X, Q, R, not_27_out);
  or or_1 (Y, and_1_out, and_2_out);
  or or_2 (or_2_out, and_3_out, and_4_out, and_5_out);
  or or_3 (or_3_out, and_6_out, and_7_out, and_8_out, and_9_out, and_10_out);
  Clock clock_1 (.out(clock_1_out));
  or or_4 (or_4_out, and_11_out, and_12_out, and_13_out, and_14_out, and_15_out, and_16_out);
  or or_5 (or_5_out, and_17_out, and_18_out, and_19_out, P, and_20_out, and_21_out, and_22_out);
  D_Flip_Flop u_P (.clk(clock_1_out), .D(or_2_out), .Q(P));  // open: Qn, preset, en, reset
  D_Flip_Flop u_Q (.clk(clock_1_out), .D(or_3_out), .Q(Q));  // open: Qn, preset, en, reset
  D_Flip_Flop u_R (.clk(clock_1_out), .D(or_4_out), .Q(R));  // open: Qn, preset, en, reset
  D_Flip_Flop u_S (.clk(clock_1_out), .D(or_5_out), .Q(S));  // open: Qn, preset, en, reset

  // Notes on the sheet:
  //   Output akan keluar di next state.
endmodule

module No__2__Version_2 (
  input  X,
  output Y,
  output P,
  output Q,
  output R
);

  wire and_1_out, and_2_out, and_3_out, and_4_out, and_5_out, and_6_out, and_7_out, and_8_out, and_9_out,
       and_10_out, and_11_out, and_12_out, and_13_out, and_14_out, and_15_out, clock_1_out, not_1_out,
       not_2_out, not_3_out, not_4_out, not_5_out, not_6_out, not_7_out, not_8_out, not_9_out, not_10_out,
       not_11_out, not_12_out, not_13_out, not_14_out, not_15_out, not_16_out, not_17_out, not_18_out,
       not_19_out, not_20_out, not_21_out, or_2_out, or_3_out, or_4_out;

  not not_1 (not_1_out, X);
  not not_2 (not_2_out, Q);
  not not_3 (not_3_out, R);
  not not_4 (not_4_out, X);
  not not_5 (not_5_out, Q);
  not not_6 (not_6_out, X);
  not not_7 (not_7_out, X);
  not not_8 (not_8_out, X);
  not not_9 (not_9_out, P);
  not not_10 (not_10_out, Q);
  not not_11 (not_11_out, P);
  not not_12 (not_12_out, Q);
  not not_13 (not_13_out, P);
  not not_14 (not_14_out, R);
  not not_15 (not_15_out, Q);
  not not_16 (not_16_out, R);
  not not_17 (not_17_out, X);
  not not_18 (not_18_out, X);
  not not_19 (not_19_out, P);
  not not_20 (not_20_out, Q);
  not not_21 (not_21_out, R);
  and and_1 (and_1_out, not_1_out, Q, R);
  and and_2 (and_2_out, X, P, not_2_out, not_3_out);
  and and_3 (and_3_out, not_4_out, not_5_out);
  and and_4 (and_4_out, not_6_out, R);
  and and_5 (and_5_out, not_7_out, P);
  and and_6 (and_6_out, P, R);
  and and_7 (and_7_out, not_8_out, not_9_out, not_10_out);
  and and_8 (and_8_out, not_11_out, not_12_out, R);
  and and_9 (and_9_out, not_13_out, Q, not_14_out);
  and and_10 (and_10_out, P, not_15_out, not_16_out);
  and and_11 (and_11_out, not_17_out, Q);
  and and_12 (and_12_out, Q, R);
  and and_13 (and_13_out, not_18_out, P, R);
  and and_14 (and_14_out, P, Q);
  and and_15 (and_15_out, X, not_19_out, not_20_out, not_21_out);
  or or_1 (Y, and_1_out, and_2_out);
  Clock clock_1 (.out(clock_1_out));
  or or_2 (or_2_out, and_3_out, and_4_out, and_5_out, and_6_out);
  or or_3 (or_3_out, and_7_out, and_8_out, and_9_out, and_10_out);
  or or_4 (or_4_out, and_11_out, and_12_out, and_13_out, and_14_out, and_15_out);
  D_Flip_Flop u_P (.clk(clock_1_out), .D(or_2_out), .Q(P));  // open: Qn, preset, en, reset
  D_Flip_Flop u_Q (.clk(clock_1_out), .D(or_3_out), .Q(Q));  // open: Qn, preset, en, reset
  D_Flip_Flop u_R (.clk(clock_1_out), .D(or_4_out), .Q(R));  // open: Qn, preset, en, reset

  // Notes on the sheet:
  //   Output akan keluar di current state.
endmodule

// C
module No__3 (
  input  X,
  output out_2
);

  wire and_1_out, and_2_out, and_3_out, and_4_out, clock_1_out, not_1_out, not_2_out, not_3_out, not_4_out,
       or_1_out, P_q, Q_q, R_q;

  Clock clock_1 (.out(clock_1_out));
  not not_1 (not_1_out, X);
  not not_2 (not_2_out, X);
  not not_3 (not_3_out, Q_q);
  not not_4 (not_4_out, X);
  and and_1 (and_1_out, Q_q, R_q, not_1_out);
  and and_2 (and_2_out, R_q, not_2_out);
  and and_3 (and_3_out, not_3_out, not_4_out);
  and and_4 (and_4_out, Q_q, X);
  or or_1 (or_1_out, and_3_out, and_4_out);
  J_K_Flip_Flop P (.J(and_1_out), .clk(clock_1_out), .K(1'b1), .Q(P_q));  // open: Qn, preset, en, reset
  J_K_Flip_Flop Q (.J(and_2_out), .clk(clock_1_out), .K(R_q), .Q(Q_q));  // open: Qn, preset, en, reset
  J_K_Flip_Flop R (.J(or_1_out), .clk(clock_1_out), .K(1'b1), .Q(R_q));  // open: Qn, preset, en, reset
  J_K_Flip_Flop j_k_ff_1 (.J(P_q), .clk(clock_1_out), .K(P_q), .Q(out_2));  // open: Qn, preset, en, reset

  // Notes on the sheet:
  //   JK Flip Flop untuk menentukan ganjil atau genap
endmodule
