// Logisim project PSD - LAB 01 - ALDEN LUTHFI - 2206128932.circ as structural Verilog: 2 circuits, main circuit Rangkaian 1
module Rangkaian_1 (
  input  A,
  input  B,
  output F___AB,
  output F___A_prime_B,
  output F___AB_prime,
  output F___A_prime_B_prime
);

  wire not_1_out, not_2_out, not_3_out, not_4_out;

  not not_1 (not_1_out, A);
  not not_2 (not_2_out, B);
  not not_3 (not_3_out, A);
  not not_4 (not_4_out, B);
  and and_1 (F___AB, B, A);
  and and_2 (F___A_prime_B, not_1_out, B);
  and and_3 (F___AB_prime, A, not_2_out);
  and and_4 (F___A_prime_B_prime, not_3_out, not_4_out);
endmodule

module Rangkaian_2 (
  input  X,
  input  Y,
  input  Z,
  input  A,
  input  B,
  output F___A_prime_B_prime_X___A_prime_B_X_Y__prime___AB_prime_Y_Z____ABZ
);

  wire and_1_out, and_2_out, and_3_out, and_4_out, not_1_out, or_1_out, or_2_out,
       rangkaian_1_1_f___a_prime_b, rangkaian_1_1_f___a_prime_b_prime, rangkaian_1_1_f___ab,
       rangkaian_1_1_f___ab_prime;

  or or_1 (or_1_out, X, Y);
  or or_2 (or_2_out, Y, Z);
  Rangkaian_1 rangkaian_1_1 (
    .A(A), .B(B), .F___AB(rangkaian_1_1_f___ab), .F___A_prime_B(rangkaian_1_1_f___a_prime_b),
    .F___AB_prime(rangkaian_1_1_f___ab_prime), .F___A_prime_B_prime(rangkaian_1_1_f___a_prime_b_prime));
  not not_1 (not_1_out, or_1_out);
  and and_1 (and_1_out, X, rangkaian_1_1_f___a_prime_b_prime);
  and and_2 (and_2_out, not_1_out, rangkaian_1_1_f___a_prime_b);
  and and_3 (and_3_out, or_2_out, rangkaian_1_1_f___ab_prime);
  and and_4 (and_4_out, Z, rangkaian_1_1_f___ab);
  or or_3 (F___A_prime_B_prime_X___A_prime_B_X_Y__prime___AB_prime_Y_Z____ABZ, and_1_out, and_2_out, and_3_out, and_4_out);

  // Notes on the sheet:
  //   Rangkaian 1
  //   X
  //   (X+Y)'
  //   (Y+Z)
  //   Z
  //   A'B'X
  //   A'B(X+Y)'
  //   AB'(Y+Z)
  //   ABZ
endmodule
