// Logisim project PSD - LAB 03 - ALDEN LUTHFI - 2206028932.circ as structural Verilog: 3 circuits, main circuit Decoder
module Decoder (
  input  A0,
  input  A1,
  output _00,
  output _01,
  output _10,
  output _11
);

  wire not_1_out, not_2_out, not_3_out, not_4_out;

  and and_1 (_00, A1, A0);
  not not_1 (not_1_out, A0);
  not not_2 (not_2_out, A1);
  not not_3 (not_3_out, A1);
  not not_4 (not_4_out, A0);
  and and_2 (_01, A1, not_1_out);
  and and_3 (_10, not_2_out, A0);
  and and_4 (_11, not_3_out, not_4_out);
endmodule

module Multiplexer (
  input  _00,
  input  _01,
  input  _10,
  input  _11,
  input  S0,
  input  S1,
  output O
);

  wire and_1_out, and_2_out, and_3_out, and_4_out, not_1_out, not_2_out, not_3_out, not_4_out;

  not not_1 (not_1_out, S0);
  not not_2 (not_2_out, S1);
  not not_3 (not_3_out, S1);
  not not_4 (not_4_out, S0);
  and and_1 (and_1_out, _00, not_1_out, not_2_out);
  and and_2 (and_2_out, _01, S0, not_3_out);
  and and_3 (and_3_out, _10, not_4_out, S1);
  and and_4 (and_4_out, _11, S0, S1);
  or or_1 (O, and_1_out, and_2_out, and_3_out, and_4_out);
endmodule

module Multiplexer_and_Decoder (
  input  A0,
  input  A1,
  input  S0,
  input  S1,
  output O
);

  wire Decoder__00, Decoder__01, Decoder__10, Decoder__11;

  Decoder Decoder (.A0(A0), .A1(A1), ._00(Decoder__00), ._01(Decoder__01), ._10(Decoder__10), ._11(Decoder__11));
  Multiplexer Multiplexer (
    ._00(Decoder__00), ._01(Decoder__01), ._10(Decoder__10), ._11(Decoder__11), .S0(S0), .S1(S1), .O(O));
endmodule
