// Logisim project PSD - LAB 02 - ALDEN LUTHFI - 2206028932.circ as structural Verilog: 2 circuits, main circuit Sebelum Dioptimasi (SOM)
module Sebelum_Dioptimasi__SOM (
  input  W,
  input  X,
  input  Y,
  input  Z,
  output O
);

  wire and_1_out, and_2_out, and_3_out, and_4_out, and_5_out, and_6_out, and_7_out, not_1_out, not_2_out,
       not_3_out, not_4_out, not_5_out, not_6_out, not_7_out, not_8_out, not_9_out, not_10_out, not_11_out,
       not_12_out, not_13_out, not_14_out, not_15_out, not_16_out, not_17_out, not_18_out;

  not not_1 (not_1_out, W);
  not not_2 (not_2_out, X);
  not not_3 (not_3_out, Y);
  not not_4 (not_4_out, W);
  not not_5 (not_5_out, X);
  not not_6 (not_6_out, Z);
  not not_7 (not_7_out, W);
  not not_8 (not_8_out, X);
  not not_9 (not_9_out, W);
  not not_10 (not_10_out, Y);
  not not_11 (not_11_out, Z);
  not not_12 (not_12_out, W);
  not not_13 (not_13_out, Z);
  not not_14 (not_14_out, X);
  not not_15 (not_15_out, Y);
  not not_16 (not_16_out, Z);
  not not_17 (not_17_out, Y);
  not not_18 (not_18_out, Z);
  and and_1 (and_1_out, not_1_out, not_2_out, not_3_out, Z);
  and and_2 (and_2_out, not_4_out, not_5_out, Y, not_6_out);
  and and_3 (and_3_out, not_7_out, not_8_out, Y, Z);
  and and_4 (and_4_out, not_9_out, X, not_10_out, not_11_out);
  and and_5 (and_5_out, not_12_out, X, Y, not_13_out);
  and and_6 (and_6_out, W, not_14_out, not_15_out, not_16_out);
  and and_7 (and_7_out, W, X, not_17_out, not_18_out);
  or or_1 (O, and_1_out, and_2_out, and_3_out, and_4_out, and_5_out, and_6_out, and_7_out);
endmodule

module Setelah_Dioptimasi (
  input  W,
  input  X,
  input  Y,
  input  Z,
  output O
);

  wire and_1_out, and_2_out, and_3_out, and_4_out, not_1_out, not_2_out, not_3_out, not_4_out, not_5_out,
       or_1_out, or_2_out;

  not not_1 (not_1_out, X);
  and and_1 (and_1_out, not_1_out, Z);
  and and_2 (and_2_out, Y, not_2_out);
  not not_2 (not_2_out, Z);
  not not_3 (not_3_out, W);
  or or_1 (or_1_out, and_1_out, and_2_out);
  not not_4 (not_4_out, Y);
  not not_5 (not_5_out, Z);
  or or_2 (or_2_out, X, W);
  and and_3 (and_3_out, not_3_out, or_1_out);
  and and_4 (and_4_out, not_4_out, not_5_out, or_2_out);
  or or_3 (O, and_3_out, and_4_out);
endmodule
