// Logisim project PSD - LAB 07 - ALDEN LUTHFI - 2206028932.circ as structural Verilog: 7 circuits, main circuit Part 1 Register A Single Cell
module Register_B (
  input  Clock,
  input  [3:0] Parrarel_load_register,
  output [3:0] Register_B_t
);

  D_Flip_Flop d_ff_1 (.clk(Clock), .D(Parrarel_load_register[0]), .Q(Register_B_t[0]));  // open: Qn, preset, en, reset
  D_Flip_Flop d_ff_2 (.clk(Clock), .D(Parrarel_load_register[1]), .Q(Register_B_t[1]));  // open: Qn, preset, en, reset
  D_Flip_Flop d_ff_3 (.clk(Clock), .D(Parrarel_load_register[2]), .Q(Register_B_t[2]));  // open: Qn, preset, en, reset
  D_Flip_Flop d_ff_4 (.clk(Clock), .D(Parrarel_load_register[3]), .Q(Register_B_t[3]));  // open: Qn, preset, en, reset
endmodule

module Part_1_Register_A_Single_Cell (
  input  S1,
  input  S0,
  input  A,
  input  B,
  input  Clock,
  output A_t
);

  wire and_1_out, and_2_out, and_3_out, not_1_out, not_2_out, not_3_out, not_4_out, not_5_out, not_6_out,
       or_1_out, or_2_out, xor_1_out;

  not not_1 (not_1_out, B);
  not not_2 (not_2_out, S0);
  not not_3 (not_3_out, S0);
  xor xor_1 (xor_1_out, A, B);
  not not_4 (not_4_out, S1);
  or or_1 (or_1_out, not_1_out, not_2_out);
  not not_5 (not_5_out, A);
  not not_6 (not_6_out, B);
  and and_1 (and_1_out, not_3_out, xor_1_out);
  and and_2 (and_2_out, not_4_out, A, or_1_out);
  and and_3 (and_3_out, S1, S0, not_5_out, not_6_out);
  or or_2 (or_2_out, and_1_out, and_2_out, and_3_out);
  D_Flip_Flop d_ff_1 (.clk(Clock), .D(or_2_out), .Q(A_t));  // open: Qn, preset, en, reset
endmodule

module Part_1_Register_A (
  input  S1,
  input  S0,
  input  [3:0] Register_B,
  input  Clock,
  output [3:0] Register_A_t
);

  Part_1_Register_A_Single_Cell A0 (
    .S1(S1), .S0(S0), .A(Register_A_t[0]), .B(Register_B[0]), .Clock(Clock), .A_t(Register_A_t[0]));
  Part_1_Register_A_Single_Cell A1 (
    .S1(S1), .S0(S0), .A(Register_A_t[1]), .B(Register_B[1]), .Clock(Clock), .A_t(Register_A_t[1]));
  Part_1_Register_A_Single_Cell A2 (
    .S1(S1), .S0(S0), .A(Register_A_t[2]), .B(Register_B[2]), .Clock(Clock), .A_t(Register_A_t[2]));
  Part_1_Register_A_Single_Cell A3 (
    .S1(S1), .S0(S0), .A(Register_A_t[3]), .B(Register_B[3]), .Clock(Clock), .A_t(Register_A_t[3]));
endmodule

module Main_Circuit_Part_1 (
  input  S1,
  input  S0,
  input  [3:0] Parallel_Load_Register_B,
  output [3:0] B_t,
  output [3:0] A_t
);

  wire clock_1_out;

  Clock clock_1 (.out(clock_1_out));
  Register_B Register_B (.Clock(clock_1_out), .Parrarel_load_register(Parallel_Load_Register_B), .Register_B_t(B_t));
  Part_1_Register_A Part_1_Register_A (.S1(S1), .S0(S0), .Register_B(B_t), .Clock(clock_1_out), .Register_A_t(A_t));
endmodule

module Part_2_Register_A_Single_Cell (
  input  A,
  input  B,
  input  [1:0] S1S0,
  input  Clock,
  output A_t
);

  wire and_1_out, multiplexer_1_out, nor_1_out, not_1_out, or_1_out, xor_1_out;

  not not_1 (not_1_out, B);
  or or_1 (or_1_out, A, B);
  and and_1 (and_1_out, A, not_1_out);
  xor xor_1 (xor_1_out, A, B);
  nor nor_1 (nor_1_out, A, B);
  Multiplexer #(.select(2)) multiplexer_1 (
    .in0(or_1_out), .in1(and_1_out), .in2(xor_1_out), .in3(nor_1_out), .out(multiplexer_1_out), .sel(S1S0));  // open: en
  D_Flip_Flop d_ff_1 (.clk(Clock), .D(multiplexer_1_out), .Q(A_t));  // open: Qn, preset, en, reset
endmodule

module Part_2_Register_A (
  input  [3:0] Register_B,
  input  Clock,
  input  [1:0] S1S0,
  output [3:0] Register_A_t
);

  Part_2_Register_A_Single_Cell part_2_register_a_single_cell_1 (
    .A(Register_A_t[0]), .B(Register_B[0]), .Clock(Clock), .S1S0(S1S0), .A_t(Register_A_t[0]));
  Part_2_Register_A_Single_Cell part_2_register_a_single_cell_2 (
    .A(Register_A_t[1]), .B(Register_B[1]), .Clock(Clock), .S1S0(S1S0), .A_t(Register_A_t[1]));
  Part_2_Register_A_Single_Cell part_2_register_a_single_cell_3 (
    .A(Register_A_t[2]), .B(Register_B[2]), .Clock(Clock), .S1S0(S1S0), .A_t(Register_A_t[2]));
  Part_2_Register_A_Single_Cell part_2_register_a_single_cell_4 (
    .A(Register_A_t[3]), .B(Register_B[3]), .Clock(Clock), .S1S0(S1S0), .A_t(Register_A_t[3]));
endmodule

module Main_Circuit_Part_2 (
  input  [3:0] Parallel_Load_Register_B,
  input  [1:0] S1S0,
  output [3:0] B_t,
  output [3:0] A_t
);

  wire clock_1_out;

  Clock clock_1 (.out(clock_1_out));
  Register_B Register_B (.Clock(clock_1_out), .Parrarel_load_register(Parallel_Load_Register_B), .Register_B_t(B_t));
  Part_2_Register_A Part_2_Register_A (.Register_B(B_t), .Clock(clock_1_out), .S1S0(S1S0), .Register_A_t(A_t));
endmodule
