// Logisim project PSD - LAB 08 - ALDEN LUTHFI - 2206028932.circ as structural Verilog: 4 circuits, main circuit Counter Circuit
module Counter_Circuit (
  input  Clock,
  input  Load,
  input  [3:0] Input,
  input  A,
  input  B,
  input  C,
  output [3:0] out_7,
  output Carryout
);

  wire and_1_out, and_2_out, and_3_out, and_4_out, and_5_out, and_6_out, and_7_out, and_8_out, and_9_out,
       and_10_out, and_11_out, and_12_out, and_13_out, and_14_out, controlled_buffer_1_out,
       controlled_buffer_3_out, not_1_out, not_2_out, not_3_out, not_4_out, not_5_out, not_6_out, or_1_out,
       or_2_out, or_3_out, or_4_out, xor_1_out, xor_2_out, xor_3_out, xor_4_out;

  not not_1 (not_1_out, Load);
  and and_1 (and_1_out, Load, Input[0]);
  or or_1 (or_1_out, and_1_out, and_2_out);
  and and_2 (and_2_out, not_1_out, xor_1_out);
  and and_3 (and_3_out, Load, Input[1]);
  or or_2 (or_2_out, and_3_out, and_4_out);
  and and_4 (and_4_out, not_1_out, xor_2_out);
  and and_5 (and_5_out, Load, Input[2]);
  or or_3 (or_3_out, and_5_out, and_6_out);
  and and_6 (and_6_out, not_1_out, xor_3_out);
  and and_7 (and_7_out, Load, Input[3]);
  or or_4 (or_4_out, and_7_out, and_8_out);
  and and_8 (and_8_out, xor_4_out, not_1_out);
  not not_2 (not_2_out, B);
  not not_3 (not_3_out, C);
  not not_4 (not_4_out, C);
  and and_9 (and_9_out, A, C);
  D_Flip_Flop d_ff_1 (.clk(Clock), .D(or_1_out), .Q(out_7[0]));  // open: Qn, preset, en, reset
  D_Flip_Flop d_ff_2 (.clk(Clock), .D(or_2_out), .Q(out_7[1]));  // open: Qn, preset, en, reset
  D_Flip_Flop d_ff_3 (.clk(Clock), .D(or_3_out), .Q(out_7[2]));  // open: Qn, preset, en, reset
  D_Flip_Flop d_ff_4 (.clk(Clock), .D(or_4_out), .Q(out_7[3]));  // open: Qn, preset, en, reset
  and and_10 (and_10_out, A, not_2_out, not_3_out);
  and and_11 (and_11_out, A, B, not_4_out);
  and and_12 (and_12_out, out_7[0], and_10_out);
  not not_5 (not_5_out, and_11_out);
  assign controlled_buffer_1_out = not_5_out ? and_12_out : 1'bz;  // Controlled_Buffer controlled_buffer_1
  assign controlled_buffer_1_out = and_11_out ? and_11_out : 1'bz;  // Controlled_Buffer controlled_buffer_2
  and and_13 (and_13_out, out_7[1], controlled_buffer_1_out);
  not not_6 (not_6_out, and_9_out);
  assign controlled_buffer_3_out = not_6_out ? and_13_out : 1'bz;  // Controlled_Buffer controlled_buffer_3
  assign controlled_buffer_3_out = and_9_out ? and_9_out : 1'bz;  // Controlled_Buffer controlled_buffer_4
  and and_14 (and_14_out, out_7[2], controlled_buffer_3_out);
  and and_15 (Carryout, out_7[3], and_14_out);
  xor xor_1 (xor_1_out, and_10_out, out_7[0]);
  xor xor_2 (xor_2_out, controlled_buffer_1_out, out_7[1]);
  xor xor_3 (xor_3_out, controlled_buffer_3_out, out_7[2]);
  xor xor_4 (xor_4_out, and_14_out, out_7[3]);
endmodule

module Counter (
  input  Load,
  input  [3:0] Input,
  input  Counter,
  input  Inc_2,
  input  Inc_4
);

  wire clock_1_out;
  wire [3:0] counter_circuit_1_out_7;

  Clock clock_1 (.out(clock_1_out));
  Counter_Circuit counter_circuit_1 (
    .Clock(clock_1_out), .Load(Load), .Input(Input), .A(Counter), .B(Inc_2), .C(Inc_4),
    .out_7(counter_circuit_1_out_7));  // open: Carryout
  Hex_Digit_Display hex_digit_display_1 (.value(counter_circuit_1_out_7));  // open: dp
endmodule

module _4_Digit_Counter_Circuit (
  input  in_1,
  input  Load,
  input  Counter,
  input  Inc_2,
  input  Inc_4,
  input  [3:0] Input,
  input  [3:0] Input_2,
  input  [3:0] Input_3,
  input  [3:0] Input_4,
  output [3:0] out_10,
  output [3:0] out_11,
  output [3:0] out_12,
  output [3:0] out_13
);

  wire counter_circuit_1_carryout, counter_circuit_2_carryout, counter_circuit_3_carryout;

  Counter_Circuit counter_circuit_1 (
    .Clock(in_1), .Load(Load), .Input(Input), .A(Counter), .B(Inc_2), .C(Inc_4), .out_7(out_10),
    .Carryout(counter_circuit_1_carryout));
  Hex_Digit_Display hex_digit_display_1 (.value(out_10));  // open: dp
  Counter_Circuit counter_circuit_2 (
    .Clock(in_1), .Load(Load), .Input(Input_2), .A(counter_circuit_1_carryout), .B(1'b0), .C(1'b0),
    .out_7(out_11), .Carryout(counter_circuit_2_carryout));
  Hex_Digit_Display hex_digit_display_2 (.value(out_11));  // open: dp
  Counter_Circuit counter_circuit_3 (
    .Clock(in_1), .Load(Load), .Input(Input_3), .A(counter_circuit_2_carryout), .B(1'b0), .C(1'b0),
    .out_7(out_12), .Carryout(counter_circuit_3_carryout));
  Hex_Digit_Display hex_digit_display_3 (.value(out_12));  // open: dp
  Counter_Circuit counter_circuit_4 (
    .Clock(in_1), .Load(Load), .Input(Input_4), .A(counter_circuit_3_carryout), .B(1'b0), .C(1'b0),
    .out_7(out_13));  // open: Carryout
  Hex_Digit_Display hex_digit_display_4 (.value(out_13));  // open: dp
endmodule

module _4_Digit_Counter (
  input  Load,
  input  Counter,
  input  Inc_2,
  input  Inc_4,
  input  [3:0] Input_0,
  input  [3:0] Input_1,
  input  [3:0] Input_2,
  input  [3:0] Input_3
);

  wire Clock_out;
  wire [3:0] n4_digit_counter_circuit_1_out_10, n4_digit_counter_circuit_1_out_11,
       n4_digit_counter_circuit_1_out_12, n4_digit_counter_circuit_1_out_13;

  Hex_Digit_Display hex_digit_display_1 (.value(Input_3));  // open: dp
  Hex_Digit_Display hex_digit_display_2 (.value(Input_2));  // open: dp
  Hex_Digit_Display hex_digit_display_3 (.value(Input_0));  // open: dp
  Hex_Digit_Display hex_digit_display_4 (.value(Input_1));  // open: dp
  Clock Clock (.out(Clock_out));
  _4_Digit_Counter_Circuit u_4_digit_counter_circuit_1 (
    .in_1(Clock_out), .Load(Load), .Counter(Counter), .Inc_2(Inc_2), .Inc_4(Inc_4), .Input(Input_0),
    .Input_2(Input_1), .Input_3(Input_2), .Input_4(Input_3), .out_10(n4_digit_counter_circuit_1_out_10),
    .out_11(n4_digit_counter_circuit_1_out_11), .out_12(n4_digit_counter_circuit_1_out_12),
    .out_13(n4_digit_counter_circuit_1_out_13));
  Hex_Digit_Display hex_digit_display_5 (.value(n4_digit_counter_circuit_1_out_13));  // open: dp
  Hex_Digit_Display hex_digit_display_6 (.value(n4_digit_counter_circuit_1_out_12));  // open: dp
  Hex_Digit_Display hex_digit_display_7 (.value(n4_digit_counter_circuit_1_out_11));  // open: dp
  Hex_Digit_Display hex_digit_display_8 (.value(n4_digit_counter_circuit_1_out_10));  // open: dp
endmodule
