// Logisim project PSD - TUGAS MANDIRI 8 - ALDEN LUTHFI - 2206028932.circ as structural Verilog: 1 circuit, main circuit main
module main (
  input  in_1
);

  wire and_1_out, clock_1_out, d_ff_1_q, d_ff_2_q, not_1_out, xor_1_out, xor_2_out;

  Clock clock_1 (.out(clock_1_out));
  not not_1 (not_1_out, d_ff_1_q);
  xor xor_1 (xor_1_out, in_1, d_ff_1_q);
  xor xor_2 (xor_2_out, d_ff_2_q, and_1_out);
  and and_1 (and_1_out, in_1, not_1_out);
  D_Flip_Flop d_ff_1 (.clk(clock_1_out), .D(xor_1_out), .Q(d_ff_1_q));  // open: Qn, preset, en, reset
  D_Flip_Flop d_ff_2 (.clk(clock_1_out), .D(xor_2_out), .Q(d_ff_2_q));  // open: Qn, preset, en, reset
endmodule
