// Logisim project PSD - LAB 04 - ALDEN LUTHFI - 2206028932.circ as structural Verilog: 4 circuits, main circuit Peubah
module Peubah (
  input  [3:0] in_1,
  output [3:0] out_2
);

  wire and_1_out, and_2_out, and_3_out, and_4_out, and_5_out, and_6_out, and_7_out, and_8_out, and_9_out,
       and_10_out, and_11_out, and_12_out, not_1_out, not_2_out, not_3_out, not_4_out, not_5_out, not_6_out,
       not_7_out, not_8_out, not_9_out, not_10_out, not_11_out, not_12_out;

  not not_1 (not_1_out, in_1[2]);
  not not_2 (not_2_out, in_1[1]);
  not not_3 (not_3_out, in_1[0]);
  not not_4 (not_4_out, in_1[2]);
  not not_5 (not_5_out, in_1[3]);
  not not_6 (not_6_out, in_1[0]);
  not not_7 (not_7_out, in_1[1]);
  not not_8 (not_8_out, in_1[3]);
  not not_9 (not_9_out, in_1[0]);
  and and_1 (and_1_out, in_1[3], not_1_out);
  and and_2 (and_2_out, in_1[3], not_2_out);
  and and_3 (and_3_out, in_1[3], not_3_out);
  not not_10 (not_10_out, in_1[3]);
  and and_4 (and_4_out, not_10_out, in_1[2]);
  and and_5 (and_5_out, in_1[2], not_11_out);
  not not_11 (not_11_out, in_1[1]);
  and and_6 (and_6_out, in_1[2], not_12_out);
  not not_12 (not_12_out, in_1[0]);
  and and_7 (and_7_out, in_1[3], not_4_out, in_1[1], in_1[0]);
  and and_8 (and_8_out, not_5_out, in_1[1]);
  and and_9 (and_9_out, in_1[1], not_6_out);
  and and_10 (and_10_out, in_1[3], not_7_out, in_1[0]);
  and and_11 (and_11_out, not_8_out, in_1[0]);
  and and_12 (and_12_out, in_1[3], not_9_out);
  or or_1 (out_2[3], and_1_out, and_2_out, and_3_out);
  or or_2 (out_2[1], and_8_out, and_9_out, and_10_out);
  or or_3 (out_2[0], and_11_out, and_12_out);
  or or_4 (out_2[2], and_4_out, and_5_out, and_6_out, and_7_out);
endmodule

module Main_Circuit (
  input  [3:0] in_1,
  input  [3:0] in_2,
  output Overflow,
  output [3:0] Sum__2s_Complement
);

  wire [3:0] Peubah_2_out_2, Peubah_out_2;

  Peubah Peubah (.in_1(in_1), .out_2(Peubah_out_2));
  _4_Bit_Parrarel_Full_Adder _4_Bit_Parrarel_Adder (
    .Overflow(Overflow), .A(Peubah_out_2), .B(Peubah_2_out_2), .Sum(Sum__2s_Complement));
  Peubah Peubah_2 (.in_1(in_2), .out_2(Peubah_2_out_2));
endmodule

module _4_Bit_Parrarel_Full_Adder (
  input  [3:0] A,
  input  [3:0] B,
  output Overflow,
  output [3:0] Sum
);

  wire n1_bit_full_adder_1_carry_out, n1_bit_full_adder_2_carry_out, n1_bit_full_adder_3_carry_out,
       n1_bit_full_adder_4_carry_out;

  _1_Bit_Full_Adder u_1_bit_full_adder_1 (
    .X(B[0]), .Y(A[0]), .Carry_in(1'b0), .Sum(Sum[0]), .Carry_out(n1_bit_full_adder_1_carry_out));
  _1_Bit_Full_Adder u_1_bit_full_adder_2 (
    .X(A[1]), .Y(B[1]), .Carry_in(n1_bit_full_adder_1_carry_out), .Sum(Sum[1]),
    .Carry_out(n1_bit_full_adder_2_carry_out));
  _1_Bit_Full_Adder u_1_bit_full_adder_3 (
    .X(A[2]), .Y(B[2]), .Carry_in(n1_bit_full_adder_2_carry_out), .Sum(Sum[2]),
    .Carry_out(n1_bit_full_adder_3_carry_out));
  _1_Bit_Full_Adder u_1_bit_full_adder_4 (
    .X(B[3]), .Y(A[3]), .Carry_in(n1_bit_full_adder_3_carry_out), .Sum(Sum[3]),
    .Carry_out(n1_bit_full_adder_4_carry_out));
  xor xor_1 (Overflow, n1_bit_full_adder_4_carry_out, n1_bit_full_adder_3_carry_out);
endmodule

module _1_Bit_Full_Adder (
  input  X,
  input  Y,
  input  Carry_in,
  output Sum,
  output Carry_out
);

  wire and_1_out, and_2_out, xor_1_out;

  xor xor_1 (xor_1_out, X, Y);
  and and_1 (and_1_out, X, Y);
  xor xor_2 (Sum, xor_1_out, Carry_in);
  and and_2 (and_2_out, xor_1_out, Carry_in);
  or or_1 (Carry_out, and_2_out, and_1_out);
endmodule
