// Logisim project PSD - LAB 05 - ALDEN LUTHFI - 2206028932.circ as structural Verilog: 1 circuit, main circuit main
module main (
  input  Z,
  output Y
);

  wire A_q, and_1_out, and_2_out, B_q, clock_1_out, not_1_out, not_2_out, not_3_out, or_1_out, or_2_out;

  Clock clock_1 (.out(clock_1_out));
  not not_1 (not_1_out, Z);
  or or_1 (or_1_out, B_q, A_q);
  not not_2 (not_2_out, A_q);
  and and_1 (and_1_out, not_2_out, not_3_out);
  not not_3 (not_3_out, B_q);
  D_Flip_Flop A (.clk(clock_1_out), .D(and_2_out), .Q(A_q));  // open: Qn, preset, en, reset
  and and_2 (and_2_out, or_1_out, not_1_out);
  D_Flip_Flop B (.clk(clock_1_out), .D(or_2_out), .Q(B_q));  // open: Qn, preset, en, reset
  or or_2 (or_2_out, and_1_out, Z);
  and and_3 (Y, A_q, Z);
endmodule
