// Logisim project PSD - TUGAS MANDIRI 5 - ALDEN LUTHFI - 2206028932.circ as structural Verilog: 4 circuits, main circuit One Bit Adder
module One_Bit_Adder (
  input  in_1,
  input  in_2,
  input  in_3,
  output out_4,
  output out_5
);

  wire and_1_out, and_2_out, xor_1_out;

  xor xor_1 (xor_1_out, in_2, in_1);
  and and_1 (and_1_out, in_2, in_1);
  xor xor_2 (out_4, xor_1_out, in_3);
  and and_2 (and_2_out, xor_1_out, in_3);
  or or_1 (out_5, and_2_out, and_1_out);
endmodule

module Four_Bit_Adder (
  input  [3:0] in_1,
  input  Sub,
  input  [3:0] in_3,
  output Overflow,
  output [3:0] out_5
);

  wire one_bit_adder_1_out_5, one_bit_adder_2_out_5, one_bit_adder_3_out_5, one_bit_adder_4_out_5, xor_1_out,
       xor_2_out, xor_3_out, xor_4_out;

  xor xor_1 (xor_1_out, in_1[0], Sub);
  One_Bit_Adder one_bit_adder_1 (
    .in_3(Sub), .in_1(in_3[0]), .in_2(xor_1_out), .out_4(out_5[0]), .out_5(one_bit_adder_1_out_5));
  xor xor_2 (xor_2_out, in_1[1], Sub);
  One_Bit_Adder one_bit_adder_2 (
    .in_3(one_bit_adder_1_out_5), .in_1(in_3[1]), .in_2(xor_2_out), .out_4(out_5[1]),
    .out_5(one_bit_adder_2_out_5));
  xor xor_3 (xor_3_out, in_1[2], Sub);
  One_Bit_Adder one_bit_adder_3 (
    .in_3(one_bit_adder_2_out_5), .in_1(in_3[2]), .in_2(xor_3_out), .out_4(out_5[2]),
    .out_5(one_bit_adder_3_out_5));
  xor xor_4 (xor_4_out, in_1[3], Sub);
  One_Bit_Adder one_bit_adder_4 (
    .in_3(one_bit_adder_3_out_5), .in_1(in_3[3]), .in_2(xor_4_out), .out_4(out_5[3]),
    .out_5(one_bit_adder_4_out_5));
  xor xor_5 (Overflow, one_bit_adder_4_out_5, one_bit_adder_3_out_5);
endmodule

module _2s_to_SM_Converter (
  input  [3:0] in_1,
  input  in_2,
  input  [3:0] in_3,
  output Overflow,
  output [3:0] out_5
);

  wire and_1_out, four_bit_adder_1_overflow, multiplexer_1_out, not_1_out;
  wire [2:1] four_bit_adder_1_out_5;

  or or_1 (out_5[2], out_5[3], four_bit_adder_1_out_5[2]);
  Four_Bit_Adder four_bit_adder_1 (
    .in_1(in_1), .Sub(in_2), .in_3(in_3), .out_5({out_5[3], four_bit_adder_1_out_5, out_5[0]}),
    .Overflow(four_bit_adder_1_overflow));
  and and_1 (and_1_out, out_5[3], out_5[0]);
  xor xor_1 (out_5[1], four_bit_adder_1_out_5[1], and_1_out);
  not not_1 (not_1_out, out_5[0]);
  Multiplexer #(.select(3), .enable("false")) multiplexer_1 (
    .in0(1'b0), .in1(1'b0), .in2(1'b0), .in3(1'b0), .in4(not_1_out), .in5(1'b0), .in6(1'b0), .in7(1'b0),
    .out(multiplexer_1_out), .sel({out_5[3], four_bit_adder_1_out_5}));
  or or_2 (Overflow, four_bit_adder_1_overflow, multiplexer_1_out);
endmodule

module Final_Circuit (
  input  [3:0] B__2s_Complement,
  input  Substractor,
  input  [3:0] A__2s_Complement,
  output Overflow,
  output [3:0] A___B__Sign_Magnitude
);

  _2s_to_SM_Converter u_2s_to_sm_converter_1 (
    .in_1(B__2s_Complement), .in_2(Substractor), .in_3(A__2s_Complement), .out_5(A___B__Sign_Magnitude),
    .Overflow(Overflow));
endmodule
